# Fritzing sketch SmartShutter (saved by Fritzing 0.9.3b)
breadboards: 1

parts:
  Q1 = LTR-301 [package=ltr-301]
  R1 = Trimmer Potentiometer [maximum_resistance=100kΩ package=THT]
  OptoFocus = Optocoupler [package=THT]
  OptoTrigger = Optocoupler [package=THT]
  LED1 = smd LED [color="Red (633nm)" package="0603 [SMD]"]
  R2 = Resistor [tolerance=±5% resistance=220 package=THT]
  LED2 = smd LED [color="Green (555nm)" package="0603 [SMD]"]
  R3 = Resistor [tolerance=±5% resistance=100k package=THT]
  R4 = Resistor [tolerance=±5% resistance=10k package=THT]
  R5 = Resistor [tolerance=±5% resistance=10k package=THT]
  U1 = 2.5mm Audio Jack [package=stereojack2.5mm_stereojack2.5mm]
  R6 = Resistor [tolerance=±5% resistance=10k package=THT]
  Composant1 = Arduino Uno (Rev3)
  Composant2 = OLED Monochrome 128x64 0.96 inch [part_number=326]
  Mode = Pushbutton [package="[THT]"]
  R7 = Resistor [tolerance=±5% resistance=10k package=THT]
  R8 = Resistor [tolerance=±5% resistance=10k package=THT]
  Set = Pushbutton [package="[THT]"]

nets:
  N1: Q1.C, R6.Pin_0, Composant1.A0
  5V: Q1.E, R1.leg2, Composant1.5V, Composant2.VIN, Mode.Pin_3, Mode.Pin_4, Set.Pin_3, Set.Pin_4
  GND: R1.leg1, OptoFocus.Pin_2, OptoTrigger.Pin_2, R2.Pin_1, R3.Pin_1, R6.Pin_1, Composant1.GND, Composant2.GND, R7.Pin_1, R8.Pin_1
  N2: R1.wiper, Composant1.A1
  N3: OptoFocus.Pin_1, R4.Pin_1
  N4: OptoFocus.Pin_4, OptoTrigger.Pin_4, U1.SLEEVE
  N5: OptoFocus.Pin_5, U1.RIGHT
  N6: OptoTrigger.Pin_1, R5.Pin_1
  N7: OptoTrigger.Pin_5, U1.LEFT
  N8: LED1.cathode, Composant1.D5_PWM
  N9: LED1.anode, R2.Pin_0
  N10: LED2.cathode, Composant1.D4
  N11: LED2.anode, R3.Pin_0
  N12: R4.Pin_0, Composant1.D10_PWM/SS
  N13: R5.Pin_0, Composant1.D11_PWM/MOSI
  N14: Composant1.A4/SDA, Composant2.MOSI_SDA
  N15: Composant1.A5/SCL, Composant2.SCLK_SCK
  N16: Composant1.D2, R8.Pin_0, Set.Pin_1, Set.Pin_2
  N17: Composant1.D3_PWM, Mode.Pin_1, Mode.Pin_2, R7.Pin_0

custom parts:
  OLED Monochrome 128x64 0.96 inch: These displays are small, only about 1" diameter, but very readable due to the high contrast of an OLED display. This display is made of 128x64 individual white OLED pixels, each one is turned on or off by the controller chip. Because the display makes its own light, no backlight is required. This reduces the power required to run the OLED and is why the display has such high contrast; we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
